# Fritzing sketch Data-Acq (saved by Fritzing 0.9.2b)
circuit board: 7.18895cm x 3.42028cm
breadboards: 1

parts:
  Raspberry_Pi1 = Raspberry Pi B+
  IC1 = MCP3008 8-channel 10-bit ADC [part_number=MCP3008]
  T1 = TMP36 Temperature Sensor [package="TO92 [THT]"]
  T2 = TMP36 Temperature Sensor [package="TO92 [THT]"]
  T3 = TMP36 Temperature Sensor [package="TO92 [THT]"]
  T4 = TMP36 Temperature Sensor [package="TO92 [THT]"]

nets (from the schematic view):
  3V3: Raspberry_Pi1.3v3, Raspberry_Pi1.3V3, IC1.no_name_yet#15, IC1.no_name_yet#16, T1.+Vs, T2.+Vs, T3.+Vs, T4.+Vs
  GND: Raspberry_Pi1.GND, IC1.no_name_yet#9, IC1.no_name_yet#14, T1.GND, T2.GND, T3.GND, T4.GND
  N1: Raspberry_Pi1.GPIO25, IC1.no_name_yet#10
  N2: Raspberry_Pi1.GPIO24, IC1.no_name_yet#11
  N3: Raspberry_Pi1.GPIO23, IC1.no_name_yet#12
  N4: Raspberry_Pi1.GPIO18, IC1.no_name_yet#13
  N5: IC1.no_name_yet#1, T1.Vout
  N6: IC1.no_name_yet#2, T2.Vout
  N7: IC1.no_name_yet#3, T3.Vout
  N8: IC1.no_name_yet#4, T4.Vout
